# Fritzing sketch pcb_full (saved by Fritzing 1.0.6)
circuit board: 12cm x 7.2cm
breadboards: 3

parts:
  LCD1 = LCD screen [part_number=1602A]
  T-sensor = female pin header, 4 pins [form="♀ (female)"]
  K1 = IC, DIP package, 10 pins [chip_label=P5]
  Q1 = NPN-Transistor [mn=2N2222 package="TO92 [THT]"]
  Q2 = NPN-Transistor [package="TO92 [THT]"]
  Q3 = NPN-Transistor [part_number=2N2222 package="TO92 [THT]"]
  R6 = Resistor [tolerance=±5% power=0.25W resistance=330 package=THT]
  R3 = Resistor [tolerance=±5% power=0.25W resistance=680 package=THT]
  R2 = Resistor [tolerance=±5% power=0.25W resistance=680 package=THT]
  R7 = Resistor [tolerance=±5% power=0.25W resistance=330 package=THT]
  S1* = SPST Switch [package=switch-spdt_lock.007s]
  R5* = Resistor [tolerance=±5% power=0.25W resistance=6.8k package=THT]
  R4* = Resistor [tolerance=±5% power=0.25W resistance=6.8k package=THT]
  S2 = Pushbutton [package="[THT]"]
  S3 = Pushbutton [package="[THT]"]
  nano = Arduino Nano (Rev3.0)
  J_LEDs = female pin header, 4 pins [form="♀ (female)"]
  R1 = Resistor [tolerance=±5% power=0.25W resistance=680 package=THT]
  D1 = Rectifier Diode [part_number=1N4001 package="300 mil [THT]"]
  D2 = Rectifier Diode [part_number=1N4001 package="300 mil [THT]"]
  D3 = Rectifier Diode [part_number=1N4001 mn=- package="300 mil [THT]"]
  C2 = Capacitor Polarized [part_number="100 uF" package=cpol-radial-100uf-25v]
  R-switch = female pin header, 3 pins [form="♀ (female)"]
  C1 = Capacitor Polarized [part_number="470 uF" package=cpol-radial-100uf-25v]
  F1 = Resettable Fuse PTC [part_number="500 mA" package=ptc]
  Buzz = Piezo Speaker
  J_rails = female pin header, 2 pins [form="♀ (female)"]
  R8 = TRIMPOT [maximum_resistance=10kΩ knob_status=50% power=0.5W package=trim_pot_pth]
  J1_12V = Power Jack [package=power_jack_pth_lock]
  R9 = Resistor [tolerance=±10% resistance=0 power=0.5W part_number="0.5 / 1W" package="2512 [SMD]"]
  R10 = Resistor [tolerance=±5% power=0.25W resistance=1k package=THT]
  R11* = Slide Potentiometer [maximum_resistance=100kΩ knob_status=50% power=0.5W]
  C3 = Capacitor [part_number=5nF package=cap-pth-5mm]

nets (from the schematic view):
  N1: LCD1.VSS, LCD1.R/W, R8.CW
  5V: LCD1.VDD, T-sensor.pin2, R7.Pin_1, S1*.O, R4*.Pin_1, nano.5V, C2.+, R8.CCW, R11*.leg2
  N2: LCD1.V0, R8.WIPER
  N3: LCD1.RS, nano.D6
  N4: LCD1.E, nano.D7
  N5: LCD1.DB4, nano.D8
  N6: LCD1.DB5, nano.D10
  N7: LCD1.DB6, nano.D11/MOSI
  N8: LCD1.DB7, nano.D12/MISO
  N9: LCD1.LED+, R7.Pin_0
  GND: LCD1.LED-, T-sensor.pin4, K1.pin10, Q2.E, Q3.E, S1*.S, R5*.Pin_1, S2.Pin_3, S2.Pin_4, S3.Pin_3, S3.Pin_4, nano.GND, J_LEDs.pin4, C2.-, C1.-, Buzz.pin1, J1_12V.GND, J1_12V.GNDBREAK, R9.Pin_0, R11*.leg1, C3.1
  N10: T-sensor.pin1, nano.D9
  N11: T-sensor.pin3, nano.D2
  N12: K1.pin1, nano.D4
  N13: K1.pin2, K1.pin7, Q1.C, D1.anode
  N14: K1.pin3, J_rails.pin1
  N15: K1.pin4, K1.pin9, nano.VIN, D1.cathode, D2.cathode, D3.cathode, R-switch.pin3, C1.+, F1.1, F1.2, J1_12V.PWR
  N16: K1.pin8, J_rails.pin2
  N17: Q1.E, R9.Pin_1, R10.Pin_0
  N18: Q1.B, R1.Pin_1
  N19: Q2.B, R2.Pin_1
  N20: Q2.C, D2.anode, R-switch.pin2
  N21: Q3.B, R3.Pin_1
  N22: Q3.C, D3.anode, R-switch.pin1
  N23: R6.Pin_0, nano.D3
  N24: R6.Pin_1, Buzz.pin2
  N25: R3.Pin_0, nano.A1
  N26: R2.Pin_0, nano.A0
  N27: S1*.P, R5*.Pin_0, R4*.Pin_0, nano.A6, R11*.wiper
  N28: S2.Pin_1, S2.Pin_2, nano.A4
  N29: S3.Pin_1, S3.Pin_2, nano.A5
  N30: nano.D5, R1.Pin_0
  N31: nano.A7, R10.Pin_1, C3.2
  N32: nano.A3, J_LEDs.pin3
  N33: nano.A2, J_LEDs.pin2
  N34: nano.D13/SCK, J_LEDs.pin1

notes:
  github.com/vaddieg
  Train control v0.3
  miniUSB
  +
  GND
  R
  L
  5V
  beam
  _/\/\/\_
  TOS
  **35mm slider
  R11**
  ANALOG_THROTTLE
  *Discrete throttle
  (default)
  option
